# Fritzing sketch Montage PMF (saved by Fritzing 0.9.3b)
breadboards: 1

parts:
  Q1 = PNP-Transistor [package="TO92 [THT]"]
  Composant1 = Arduino Uno (Rev3)
  RHT1 = Humidity and Temperature Sensor RHT03
  RHT2 = Humidity and Temperature Sensor RHT03
  R1 = Resistor [tolerance=±5% resistance=220 package=THT]
  R2 = Resistor [tolerance=±5% resistance=220 package=THT]
  Mod1 = KY-019 5V Relay Module [package="Breakout board"]
  J1 = Peltier Element
  VCC1 = Battery

nets:
  N1: Q1.E, RHT1.GND_1, RHT2.Vcc, RHT2.GND_1, Mod1.-
  N2: Q1.B, Composant1.D7
  N3: Q1.C, Mod1.S
  N4: Composant1.D2, R1.Pin_1
  N5: Composant1.D4, R2.Pin_1
  N6: Composant1.5V, Mod1.+
  N7: RHT1.Vcc, RHT1.Data-signal, R1.Pin_0
  N8: RHT2.Data-signal, R2.Pin_0
  N9: Mod1.Common, VCC1.+
  N10: Mod1.NO, J1.pin2

notes:
  Capteur DHT22 à l'intérieur du frigo
  Capteur DHT22 à l'extériueur du frigo
  Relais electronique
  Module Peltier
  Alimentation de 5V

custom parts:
  KY-019 5V Relay Module: KY-019 5V Relay module, used to control AC circuits. (Special thanks to vanepp for fixing the PCB holes and other errors)
